# Fritzing sketch Blinds (saved by Fritzing 0.9.3b)
circuit board: 8.46667cm x 5.64444cm

parts:
  U1 = NodeMCU V1.0
  M1 = DC Motor
  KY-1 = Keyes Relay [package=THT]
  KY-2 = Keyes Relay [package=THT]
  VCC1 = 4 x AAA Battery Mount
  U2 = mystery part, 3 pins [chip_label="Charging Circuit"]
  Power_plug1 = Power plug

nets:
  N1: U1.D0, KY-1.signal
  N2: U1.D1, KY-2.signal
  GND: U1.GND, KY-1.ground, KY-1.NC, KY-2.ground, KY-2.NC, VCC1.-, U2.pin3, Power_plug1.GND
  N3: U1.Vin, KY-1.power, KY-1.NO, KY-2.power, KY-2.NO, VCC1.+, U2.pin1
  N4: M1.pin_1, KY-1.C
  N5: M1.pin_2, KY-2.C
  N6: U2.pin2, Power_plug1.VCC

custom parts:
  NodeMCU V1.0: ESP8266 based NodeMCU
  Keyes Relay: The Keyes 5V relay module is suitable for SCM development, home appliance control. It uses a 5V~12V TIL control signal which can control DC / AC signal.
